# Fritzing sketch auto-plant-watering-board-mkr1000 (saved by Fritzing 0.9.3b)
circuit board: 9.81797cm x 5.38952cm
stripboards: 1

parts:
  V_Reg = Voltage Regulator - 5V [package="TO220 [THT]"]
  LED = LED - 5mm [color="Red (633nm)" package="5 mm [THT]"]
  MOSFET = Basic FET N-Channel [package="TO220 [THT]"]
  1N4001 = Schottky Diode [part_number=1N4001 breakdown_voltage=3.6V package="300 mil [THT]"]
  Pwr_Spply = Screw terminal - 2 pins [package=THT]
  Pump = Screw terminal - 2 pins [package=THT]
  To_Sensor = screw terminal, 3 pins
  150_Ohm_1 = Resistor [tolerance=±5% resistance=150 package=THT]
  Part2 = Arduino MKR1000
  150_Ohm_2 = Resistor [tolerance=±5% resistance=150 package=THT]

nets:
  N1: V_Reg.input_voltage, 1N4001.cathode, Pwr_Spply.pin1, Pump.pin2
  GND: V_Reg.GND, LED.cathode, MOSFET.source, Pwr_Spply.pin2, To_Sensor.pin3, Part2.GND
  N2: V_Reg.output_voltage, Part2.VIN
  N3: LED.anode, 150_Ohm_2.Pin_0
  N4: MOSFET.gate, 150_Ohm_1.Pin_0
  N5: MOSFET.drain, 1N4001.anode, Pump.pin1
  N6: To_Sensor.pin1, Part2.A1
  N7: To_Sensor.pin2, Part2.VCC
  N8: 150_Ohm_1.Pin_1, Part2.D8_MOSI
  N9: Part2.D10_MISO, 150_Ohm_2.Pin_1

notes:
  Arduino MKR 1000
  Analog Sensor Pump Control
  WAM 2020
  +
  -
  D

custom parts:
  Arduino MKR1000: MKR1000 is a powerful board that combines the functionality of the Zero and the Wi-Fi Shield. It is the ideal solution for makers wanting to design IoT projects with minimal previous experience in networking
